# Fritzing sketch Devre (saved by Fritzing 0.8.7b)
breadboards: 1

parts:
  S2 = Pushbutton [package="[THT]"]
  S3 = Pushbutton [package="[THT]"]
  LED1 = LED - 5mm [color="Green (570nm)" package="5 mm [THT]"]
  LED2 = LED - 5mm [color="Yellow (595nm)" package="5 mm [THT]"]
  LED3 = LED - 5mm [color="Red (633nm)" package="5 mm [THT]"]
  R3 = Resistor [tolerance=±5% resistance=220 package=THT]
  Eleman1 = Arduino Uno (Rev3)
  R4 = Resistor [tolerance=±5% resistance=220 package=THT]
  R5 = Resistor [tolerance=±5% resistance=220 package=THT]
  R6 = Resistor [tolerance=±5% resistance=10k package=THT]
  R7 = Resistor [tolerance=±5% resistance=10k package=THT]

nets:
  N1: S2.Pin_1, S2.Pin_2, Eleman1.D6_PWM, R7.Pin_1
  N2: S2.Pin_3, S2.Pin_4, S3.Pin_3, S3.Pin_4, Eleman1.5V
  N3: S3.Pin_1, S3.Pin_2, Eleman1.D7, R6.Pin_1
  N4: LED1.cathode, R3.Pin_0
  N5: LED1.anode, Eleman1.D8
  N6: LED2.cathode, R4.Pin_0
  N7: LED2.anode, Eleman1.D9_PWM
  N8: LED3.cathode, R5.Pin_0
  N9: LED3.anode, Eleman1.D10_PWM/SS
  N10: R3.Pin_1, Eleman1.3V3, R4.Pin_1, R5.Pin_1, R6.Pin_0, R7.Pin_0
